# Fritzing sketch Ultrasonic-ESP32CAM (saved by Fritzing 0.9.5d)
breadboards: 1

parts:
  ESP32_-_Back1 = ESP32 - CAM
  HC-SR04_Sensor_1 = HC-SR04 Ultrasonic Distance Sensor
  VCC1 = Battery

nets:
  N1: ESP32_-_Back1.GPIO14, HC-SR04_Sensor_1.TRIG
  N2: ESP32_-_Back1.GPIO15, HC-SR04_Sensor_1.ECHO
  N3: HC-SR04_Sensor_1.VCC, VCC1.+
  N4: HC-SR04_Sensor_1.GND, VCC1.-

custom parts:
  ESP32 - CAM: The ESP32-CAM has a very competitive small-size camera module that can operate independently as a minimum system with a footprint of only 27*40.5*4.5mm and a deep sleep current of up to 6mA.
